# Fritzing sketch test arduino raspy 4 (saved by Fritzing 0.9.6b)
breadboards: 1

parts:
  Componente1 = Arduino Nano (Rev3.0)
  Mod1 = Raspberry Pi 4B  # not connected
  LED1 = LED - 5mm [color="Red (633nm)" current=0.030 package="5 mm [THT]"]

nets:
  N1: Componente1.VIN, LED1.anode
